# Fritzing sketch EC-FAN-pid controller r2.2 (saved by Fritzing 0.9.3b)

parts:
  Part1 = Arduino Nano (Rev3.0)
  SW1 = ENCODER_RGB_CA [package=encoder_led_3]
  R1 = Resistor [tolerance=±5% resistance=4.7k package=THT]
  Mod1 = OLED Mono 0.56 inch blue or white
  R2 = Resistor [tolerance=±5% resistance=10k package=THT]
  R3 = Resistor [tolerance=±5% resistance=10k package=THT]
  R4 = Resistor [tolerance=±5% resistance=4.7k package=THT]
  R5 = Resistor [tolerance=±5% resistance=4.7k package=THT]
  R6 = Resistor [tolerance=±5% resistance=10k package=THT]
  Q1 = NPN-Transistor [part_number=BC547 package="TO92 [THT]"]
  Q2 = NPN-Transistor [part_number=BC547 package="TO92 [THT]"]
  R7 = Resistor [tolerance=±5% resistance=20k package=THT]
  R8 = Resistor [tolerance=±5% resistance=20k package=THT]
  R9 = Resistor [tolerance=±5% resistance=1k package=THT]
  R10 = Resistor [tolerance=±5% resistance=1k package=THT]
  DS1 = DS18B20 1-Wire Temperature Sensor [part_number=DS18B20]
  R12 = Resistor [tolerance=±5% resistance=4.7k part_number=4,7k package=THT]
  C4 = Electrolytic Capacitor [capacitance=0.47mF voltage=16V package="100 mil [THT, electrolytic]"]
  C1 = Ceramic Capacitor [capacitance=100nF package="100 mil [THT, multilayer]"]
  XLR1 = XLR NC3MAAH [package=nc3maah]
  TRRS1 = Audio Jack (TRRS) 3.5mm [part_number=Jack3,5 package="RC-5325A [SMD]"]

nets:
  GND: Part1.GND, SW1.+, SW1.C, Mod1.GND, Q1.E, Q2.E, DS1.GND, C4.-, C1.0, XLR1.1, TRRS1.RING2
  N1: Part1.D3, R5.Pin_1, C1.1
  N2: Part1.D7, DS1.DQ, R12.Pin_1, TRRS1.RING1
  N3: Part1.D11/MOSI, R8.Pin_0
  10V: Part1.VIN, R9.Pin_0, R10.Pin_0, C4.+, XLR1.2
  5V: Part1.5V, Mod1.VCC, R2.Pin_1, R3.Pin_0, R6.Pin_1, DS1.VDD, R12.Pin_0, TRRS1.TIP
  N4: Part1.A5, Mod1.SCL
  N5: Part1.A4, Mod1.SDA
  N6: Part1.A3, R1.Pin_1
  N7: Part1.A2, R4.Pin_1
  N8: SW1.SW, R5.Pin_0, R6.Pin_0
  N9: SW1.A, R2.Pin_0, R4.Pin_0
  N10: SW1.B, R1.Pin_0, R3.Pin_1
  N11: Q1.B, R8.Pin_1
  N12: Q1.C, R7.Pin_0, R9.Pin_1
  N13: Q2.B, R7.Pin_1
  N14: Q2.C, R10.Pin_1, XLR1.3

notes:
  0...10v signal
  +10v from FAN
  0...5v PWM
  i2c bus
  1-wire
  4,7k
  ds18b20
  jack3,5
  PIN_SW 3
  PIN_IN1 A2
  10k
  incremental encoder with switch
  A5-SCL
  bc547
  20k
  1k
  switch
  ssd1306 128x64
  oled display
  16v
  470uF
  100nF
  A4-SDA
  PIN_IN2 A3
  +5v (arduino source)
  encoder line
  common
  PWM_OUT 11
  PWM amplifier
  ONE_WIRE_BUS 7
  Arduino NANO 328 5v

custom parts:
  OLED Mono 0.56 inch blue or white: OLED, I2C 3.3V - 5V Blue and White text versions
